// Logisim project Smart_Digital_Stopwatch_System.circ as structural Verilog: 7 circuits, main circuit main
module main (
  input  SHOW_LAP_SPLIT,
  input  START_STOP,
  input  MODE_SELECT,
  input  LAP_SPLIT,
  input  RESET,
  input  in_6,
  input  LAP_FLAG,
  input  RESET_SYNC,
  output out_9,
  output out_10,
  output out_11
);

  wire and_1_out, and_2_out, and_3_out, clock_1_out, d_ff_memory_cell_1_a_2, d_ff_memory_cell_1_b_2,
       d_ff_memory_cell_1_c_2, d_ff_memory_cell_1_d_2, d_ff_memory_cell_2_a_2, d_ff_memory_cell_2_b_2,
       d_ff_memory_cell_2_c_2, d_ff_memory_cell_2_d_2, d_ff_memory_cell_3_a_2, d_ff_memory_cell_3_b_2,
       d_ff_memory_cell_3_c_2, d_ff_memory_cell_3_d_2, d_ff_memory_cell_4_a_2, d_ff_memory_cell_4_b_2,
       d_ff_memory_cell_4_c_2, d_ff_memory_cell_4_d_2, ic_74ls47_1_a__pin_13, ic_74ls47_1_b__pin_12,
       ic_74ls47_1_c___pin_11, ic_74ls47_1_d__pin_10, ic_74ls47_1_e__pin_9, ic_74ls47_1_f__pin_15,
       ic_74ls47_1_g__pin_14, ic_74ls47_2_a__pin_13, ic_74ls47_2_b__pin_12, ic_74ls47_2_c___pin_11,
       ic_74ls47_2_d__pin_10, ic_74ls47_2_e__pin_9, ic_74ls47_2_f__pin_15, ic_74ls47_2_g__pin_14,
       ic_74ls47_3_a__pin_13, ic_74ls47_3_b__pin_12, ic_74ls47_3_c___pin_11, ic_74ls47_3_d__pin_10,
       ic_74ls47_3_e__pin_9, ic_74ls47_3_f__pin_15, ic_74ls47_3_g__pin_14, ic_74ls47_4_a__pin_13,
       ic_74ls47_4_b__pin_12, ic_74ls47_4_c___pin_11, ic_74ls47_4_d__pin_10, ic_74ls47_4_e__pin_9,
       ic_74ls47_4_f__pin_15, ic_74ls47_4_g__pin_14, ic_74ls157_1__1y__pin_4, ic_74ls157_1__2y__pin_7,
       ic_74ls157_1__3y__pin_9, ic_74ls157_2__1y__pin_4, ic_74ls157_2__2y__pin_7, ic_74ls157_2__3y__pin_9,
       ic_74ls157_2__4y__pin_12, ic_74ls157_3__1y__pin_4, ic_74ls157_3__2y__pin_7, ic_74ls157_3__3y__pin_9,
       ic_74ls157_3__4y__pin_12, ic_74ls157_4__1y__pin_4, ic_74ls157_4__2y__pin_7, ic_74ls157_4__3y__pin_9,
       ic_74ls157_4__4y__pin_12, ic_74ls157_5__1y__pin_4, ic_74ls157_5__2y__pin_7, ic_74ls157_5__3y__pin_9,
       ic_74ls157_5__4y__pin_12, or_1_out, or_2_out;
  wire [3:0] ic_74ls90_1_q_a__pin_12, ic_74ls90_2_q_a__pin_12, ic_74ls90_3_q_a__pin_12,
       ic_74ls90_4_q_a__pin_12;

  Clock clock_1 (.out(clock_1_out));
  Edge_Detector edge_detector_1 (.BUTTON_INPUT(START_STOP), .PULSE_OUTPUT(out_9), .CLK(clock_1_out));
  Edge_Detector edge_detector_2 (.BUTTON_INPUT(LAP_SPLIT), .PULSE_OUTPUT(out_10), .CLK(clock_1_out));
  Edge_Detector edge_detector_3 (.BUTTON_INPUT(RESET), .PULSE_OUTPUT(out_11), .CLK(clock_1_out));
  IC_74LS157 ic_74ls157_1 (
    ._1A__PIN_2(START_STOP), ._1B__PIN_3(in_6), ._2A__PIN_5(LAP_SPLIT), ._2B__PIN_6(LAP_FLAG),
    ._3A__PIN_11(RESET), ._3B__PIN_10(RESET_SYNC), .in_9(1'b0), .in_10(MODE_SELECT),
    ._1Y__PIN_4(ic_74ls157_1__1y__pin_4), ._2Y__PIN_7(ic_74ls157_1__2y__pin_7),
    ._3Y__PIN_9(ic_74ls157_1__3y__pin_9));  // open: _4A__PIN_14, _4B__PIN_13, _4Y__PIN_12
  and and_1 (and_1_out, clock_1_out, ic_74ls157_1__1y__pin_4);
  or or_1 (or_1_out, ic_74ls157_1__3y__pin_9, and_2_out);
  and and_2 (and_2_out, ic_74ls90_2_q_a__pin_12[2], ic_74ls90_2_q_a__pin_12[1]);
  or or_2 (or_2_out, ic_74ls157_1__3y__pin_9, and_3_out);
  and and_3 (and_3_out, ic_74ls90_4_q_a__pin_12[1], ic_74ls90_4_q_a__pin_12[2]);
  IC_74LS90 ic_74ls90_1 (
    .R3__PIN_6(1'b0), .R4__PIN_7(1'b0), .R1__PIN_2(ic_74ls157_1__3y__pin_9),
    .R2__PIN_3(ic_74ls157_1__3y__pin_9), .Q_A__PIN_12(ic_74ls90_1_q_a__pin_12[0]),
    .Q_B__PIN_9(ic_74ls90_1_q_a__pin_12[1]), .Q_C__PIN_8(ic_74ls90_1_q_a__pin_12[2]),
    .Q_D__PIN_11(ic_74ls90_1_q_a__pin_12[3]), .CLK_A__PIN_14(and_1_out),
    .CLK_B__PIN_1(ic_74ls90_1_q_a__pin_12[0]), .VCC__PIN_5(1'b1));
  IC_74LS90 ic_74ls90_2 (
    .R3__PIN_6(1'b0), .R4__PIN_7(1'b0), .R1__PIN_2(or_1_out), .R2__PIN_3(or_1_out),
    .Q_A__PIN_12(ic_74ls90_2_q_a__pin_12[0]), .Q_B__PIN_9(ic_74ls90_2_q_a__pin_12[1]),
    .Q_C__PIN_8(ic_74ls90_2_q_a__pin_12[2]), .Q_D__PIN_11(ic_74ls90_2_q_a__pin_12[3]),
    .CLK_A__PIN_14(ic_74ls90_1_q_a__pin_12[3]), .CLK_B__PIN_1(ic_74ls90_2_q_a__pin_12[0]), .VCC__PIN_5(1'b1));
  IC_74LS90 ic_74ls90_3 (
    .R3__PIN_6(1'b0), .R4__PIN_7(1'b0), .R1__PIN_2(ic_74ls157_1__3y__pin_9),
    .R2__PIN_3(ic_74ls157_1__3y__pin_9), .Q_A__PIN_12(ic_74ls90_3_q_a__pin_12[0]),
    .Q_B__PIN_9(ic_74ls90_3_q_a__pin_12[1]), .Q_C__PIN_8(ic_74ls90_3_q_a__pin_12[2]),
    .Q_D__PIN_11(ic_74ls90_3_q_a__pin_12[3]), .CLK_A__PIN_14(and_2_out),
    .CLK_B__PIN_1(ic_74ls90_3_q_a__pin_12[0]), .VCC__PIN_5(1'b1));
  IC_74LS90 ic_74ls90_4 (
    .R3__PIN_6(1'b0), .R4__PIN_7(1'b0), .R1__PIN_2(or_2_out), .R2__PIN_3(or_2_out),
    .Q_A__PIN_12(ic_74ls90_4_q_a__pin_12[0]), .Q_B__PIN_9(ic_74ls90_4_q_a__pin_12[1]),
    .Q_C__PIN_8(ic_74ls90_4_q_a__pin_12[2]), .Q_D__PIN_11(ic_74ls90_4_q_a__pin_12[3]),
    .CLK_A__PIN_14(ic_74ls90_3_q_a__pin_12[3]), .CLK_B__PIN_1(ic_74ls90_4_q_a__pin_12[0]), .VCC__PIN_5(1'b1));
  D_FF_Memory_Cell d_ff_memory_cell_1 (
    .A(ic_74ls90_1_q_a__pin_12[0]), .C(ic_74ls90_1_q_a__pin_12[2]), .B(ic_74ls90_1_q_a__pin_12[1]),
    .D(ic_74ls90_1_q_a__pin_12[3]), .A_2(d_ff_memory_cell_1_a_2), .C_2(d_ff_memory_cell_1_c_2),
    .B_2(d_ff_memory_cell_1_b_2), .D_2(d_ff_memory_cell_1_d_2), .CLK(ic_74ls157_1__2y__pin_7),
    .RESET(ic_74ls157_1__3y__pin_9));
  D_FF_Memory_Cell d_ff_memory_cell_2 (
    .A(ic_74ls90_2_q_a__pin_12[0]), .C(ic_74ls90_2_q_a__pin_12[2]), .B(ic_74ls90_2_q_a__pin_12[1]),
    .D(ic_74ls90_2_q_a__pin_12[3]), .A_2(d_ff_memory_cell_2_a_2), .C_2(d_ff_memory_cell_2_c_2),
    .B_2(d_ff_memory_cell_2_b_2), .D_2(d_ff_memory_cell_2_d_2), .CLK(ic_74ls157_1__2y__pin_7),
    .RESET(ic_74ls157_1__3y__pin_9));
  D_FF_Memory_Cell d_ff_memory_cell_3 (
    .A(ic_74ls90_3_q_a__pin_12[0]), .C(ic_74ls90_3_q_a__pin_12[2]), .B(ic_74ls90_3_q_a__pin_12[1]),
    .D(ic_74ls90_3_q_a__pin_12[3]), .A_2(d_ff_memory_cell_3_a_2), .C_2(d_ff_memory_cell_3_c_2),
    .B_2(d_ff_memory_cell_3_b_2), .D_2(d_ff_memory_cell_3_d_2), .CLK(ic_74ls157_1__2y__pin_7),
    .RESET(ic_74ls157_1__3y__pin_9));
  D_FF_Memory_Cell d_ff_memory_cell_4 (
    .A(ic_74ls90_4_q_a__pin_12[0]), .C(ic_74ls90_4_q_a__pin_12[2]), .B(ic_74ls90_4_q_a__pin_12[1]),
    .D(ic_74ls90_4_q_a__pin_12[3]), .A_2(d_ff_memory_cell_4_a_2), .C_2(d_ff_memory_cell_4_c_2),
    .B_2(d_ff_memory_cell_4_b_2), .D_2(d_ff_memory_cell_4_d_2), .CLK(ic_74ls157_1__2y__pin_7),
    .RESET(ic_74ls157_1__3y__pin_9));
  IC_74LS157 ic_74ls157_2 (
    ._1A__PIN_2(ic_74ls90_1_q_a__pin_12[0]), ._1B__PIN_3(d_ff_memory_cell_1_a_2),
    ._2A__PIN_5(ic_74ls90_1_q_a__pin_12[1]), ._2B__PIN_6(d_ff_memory_cell_1_b_2),
    ._3A__PIN_11(ic_74ls90_1_q_a__pin_12[2]), ._3B__PIN_10(d_ff_memory_cell_1_c_2),
    ._4A__PIN_14(ic_74ls90_1_q_a__pin_12[3]), ._4B__PIN_13(d_ff_memory_cell_1_d_2), .in_9(1'b0),
    .in_10(SHOW_LAP_SPLIT), ._1Y__PIN_4(ic_74ls157_2__1y__pin_4), ._2Y__PIN_7(ic_74ls157_2__2y__pin_7),
    ._3Y__PIN_9(ic_74ls157_2__3y__pin_9), ._4Y__PIN_12(ic_74ls157_2__4y__pin_12));
  IC_74LS157 ic_74ls157_3 (
    ._1A__PIN_2(ic_74ls90_2_q_a__pin_12[0]), ._1B__PIN_3(d_ff_memory_cell_2_a_2),
    ._2A__PIN_5(ic_74ls90_2_q_a__pin_12[1]), ._2B__PIN_6(d_ff_memory_cell_2_b_2),
    ._3A__PIN_11(ic_74ls90_2_q_a__pin_12[2]), ._3B__PIN_10(d_ff_memory_cell_2_c_2),
    ._4A__PIN_14(ic_74ls90_2_q_a__pin_12[3]), ._4B__PIN_13(d_ff_memory_cell_2_d_2), .in_9(1'b0),
    .in_10(SHOW_LAP_SPLIT), ._1Y__PIN_4(ic_74ls157_3__1y__pin_4), ._2Y__PIN_7(ic_74ls157_3__2y__pin_7),
    ._3Y__PIN_9(ic_74ls157_3__3y__pin_9), ._4Y__PIN_12(ic_74ls157_3__4y__pin_12));
  IC_74LS157 ic_74ls157_4 (
    ._1A__PIN_2(ic_74ls90_3_q_a__pin_12[0]), ._1B__PIN_3(d_ff_memory_cell_3_a_2),
    ._2A__PIN_5(ic_74ls90_3_q_a__pin_12[1]), ._2B__PIN_6(d_ff_memory_cell_3_b_2),
    ._3A__PIN_11(ic_74ls90_3_q_a__pin_12[2]), ._3B__PIN_10(d_ff_memory_cell_3_c_2),
    ._4A__PIN_14(ic_74ls90_3_q_a__pin_12[3]), ._4B__PIN_13(d_ff_memory_cell_3_d_2), .in_9(1'b0),
    .in_10(SHOW_LAP_SPLIT), ._1Y__PIN_4(ic_74ls157_4__1y__pin_4), ._2Y__PIN_7(ic_74ls157_4__2y__pin_7),
    ._3Y__PIN_9(ic_74ls157_4__3y__pin_9), ._4Y__PIN_12(ic_74ls157_4__4y__pin_12));
  IC_74LS157 ic_74ls157_5 (
    ._1A__PIN_2(ic_74ls90_4_q_a__pin_12[0]), ._1B__PIN_3(d_ff_memory_cell_4_a_2),
    ._2A__PIN_5(ic_74ls90_4_q_a__pin_12[1]), ._2B__PIN_6(d_ff_memory_cell_4_b_2),
    ._3A__PIN_11(ic_74ls90_4_q_a__pin_12[2]), ._3B__PIN_10(d_ff_memory_cell_4_c_2),
    ._4A__PIN_14(ic_74ls90_4_q_a__pin_12[3]), ._4B__PIN_13(d_ff_memory_cell_4_d_2), .in_9(1'b0),
    .in_10(SHOW_LAP_SPLIT), ._1Y__PIN_4(ic_74ls157_5__1y__pin_4), ._2Y__PIN_7(ic_74ls157_5__2y__pin_7),
    ._3Y__PIN_9(ic_74ls157_5__3y__pin_9), ._4Y__PIN_12(ic_74ls157_5__4y__pin_12));
  IC_74LS47 ic_74ls47_1 (
    .A__PIN_7(ic_74ls157_2__1y__pin_4), .B__PIN_1(ic_74ls157_2__2y__pin_7),
    .C__PIN_2(ic_74ls157_2__3y__pin_9), .D__PIN_6(ic_74ls157_2__4y__pin_12),
    .BI_prime_RBO_prime__PIN_4(1'b0), .LT_prime__PIN_3(1'b0), .RBI_prime__PIN_5(1'b0),
    .a__PIN_13(ic_74ls47_1_a__pin_13), .b__PIN_12(ic_74ls47_1_b__pin_12),
    .c___PIN_11(ic_74ls47_1_c___pin_11), .d__PIN_10(ic_74ls47_1_d__pin_10), .e__PIN_9(ic_74ls47_1_e__pin_9),
    .f__PIN_15(ic_74ls47_1_f__pin_15), .g__PIN_14(ic_74ls47_1_g__pin_14));
  IC_74LS47 ic_74ls47_2 (
    .A__PIN_7(ic_74ls157_3__1y__pin_4), .B__PIN_1(ic_74ls157_3__2y__pin_7),
    .C__PIN_2(ic_74ls157_3__3y__pin_9), .D__PIN_6(ic_74ls157_3__4y__pin_12),
    .BI_prime_RBO_prime__PIN_4(1'b0), .LT_prime__PIN_3(1'b0), .RBI_prime__PIN_5(1'b0),
    .a__PIN_13(ic_74ls47_2_a__pin_13), .b__PIN_12(ic_74ls47_2_b__pin_12),
    .c___PIN_11(ic_74ls47_2_c___pin_11), .d__PIN_10(ic_74ls47_2_d__pin_10), .e__PIN_9(ic_74ls47_2_e__pin_9),
    .f__PIN_15(ic_74ls47_2_f__pin_15), .g__PIN_14(ic_74ls47_2_g__pin_14));
  IC_74LS47 ic_74ls47_3 (
    .A__PIN_7(ic_74ls157_4__1y__pin_4), .B__PIN_1(ic_74ls157_4__2y__pin_7),
    .C__PIN_2(ic_74ls157_4__3y__pin_9), .D__PIN_6(ic_74ls157_4__4y__pin_12),
    .BI_prime_RBO_prime__PIN_4(1'b0), .LT_prime__PIN_3(1'b0), .RBI_prime__PIN_5(1'b0),
    .a__PIN_13(ic_74ls47_3_a__pin_13), .b__PIN_12(ic_74ls47_3_b__pin_12),
    .c___PIN_11(ic_74ls47_3_c___pin_11), .d__PIN_10(ic_74ls47_3_d__pin_10), .e__PIN_9(ic_74ls47_3_e__pin_9),
    .f__PIN_15(ic_74ls47_3_f__pin_15), .g__PIN_14(ic_74ls47_3_g__pin_14));
  IC_74LS47 ic_74ls47_4 (
    .A__PIN_7(ic_74ls157_5__1y__pin_4), .B__PIN_1(ic_74ls157_5__2y__pin_7),
    .C__PIN_2(ic_74ls157_5__3y__pin_9), .D__PIN_6(ic_74ls157_5__4y__pin_12),
    .BI_prime_RBO_prime__PIN_4(1'b0), .LT_prime__PIN_3(1'b0), .RBI_prime__PIN_5(1'b0),
    .a__PIN_13(ic_74ls47_4_a__pin_13), .b__PIN_12(ic_74ls47_4_b__pin_12),
    .c___PIN_11(ic_74ls47_4_c___pin_11), .d__PIN_10(ic_74ls47_4_d__pin_10), .e__PIN_9(ic_74ls47_4_e__pin_9),
    .f__PIN_15(ic_74ls47_4_f__pin_15), .g__PIN_14(ic_74ls47_4_g__pin_14));
  _7_Segment_Display u_7_segment_display_1 (
    .g(ic_74ls47_1_g__pin_14), .f(ic_74ls47_1_f__pin_15), .a(ic_74ls47_1_a__pin_13),
    .b(ic_74ls47_1_b__pin_12), .e(ic_74ls47_1_e__pin_9), .d(ic_74ls47_1_d__pin_10), .c(ic_74ls47_1_c___pin_11));  // open: dp
  _7_Segment_Display u_7_segment_display_2 (
    .g(ic_74ls47_2_g__pin_14), .f(ic_74ls47_2_f__pin_15), .a(ic_74ls47_2_a__pin_13),
    .b(ic_74ls47_2_b__pin_12), .e(ic_74ls47_2_e__pin_9), .d(ic_74ls47_2_d__pin_10), .c(ic_74ls47_2_c___pin_11));  // open: dp
  _7_Segment_Display u_7_segment_display_3 (
    .g(ic_74ls47_3_g__pin_14), .f(ic_74ls47_3_f__pin_15), .a(ic_74ls47_3_a__pin_13),
    .b(ic_74ls47_3_b__pin_12), .e(ic_74ls47_3_e__pin_9), .d(ic_74ls47_3_d__pin_10), .c(ic_74ls47_3_c___pin_11));  // open: dp
  _7_Segment_Display u_7_segment_display_4 (
    .g(ic_74ls47_4_g__pin_14), .f(ic_74ls47_4_f__pin_15), .a(ic_74ls47_4_a__pin_13),
    .b(ic_74ls47_4_b__pin_12), .e(ic_74ls47_4_e__pin_9), .d(ic_74ls47_4_d__pin_10), .c(ic_74ls47_4_c___pin_11));  // open: dp

  // Notes on the sheet:
  //   CLK (1Hz)
  //   INPUT COMMANDS  FROM FPGA
  //   NOTE: THE PULSE INPUTS GO TO GPIO OF FPGA
  //   RUN_EN/PAUSE_EN
  //   SECOND ONES
  //   SECOND TENS
  //   MINUTE ONES
  //   MINUTE TENS
endmodule

module IC_74LS90 (
  input  VCC__PIN_5,
  input  CLK_A__PIN_14,
  input  CLK_B__PIN_1,
  input  R3__PIN_6,
  input  R4__PIN_7,
  input  R1__PIN_2,
  input  R2__PIN_3,
  output Q_A__PIN_12,
  output Q_B__PIN_9,
  output Q_C__PIN_8,
  output Q_D__PIN_11
);

  wire and_1_out, and_2_out, and_3_out, j_k_ff_4_qn, or_1_out, or_2_out;

  and and_1 (and_1_out, R3__PIN_6, R4__PIN_7);
  J_K_Flip_Flop #(.trigger("falling")) j_k_ff_1 (
    .J(VCC__PIN_5), .clk(CLK_A__PIN_14), .K(VCC__PIN_5), .Q(Q_A__PIN_12), .preset(and_1_out),
    .reset(and_3_out));  // open: Qn, en
  J_K_Flip_Flop #(.trigger("falling")) j_k_ff_2 (
    .J(j_k_ff_4_qn), .clk(CLK_B__PIN_1), .K(VCC__PIN_5), .Q(Q_B__PIN_9), .reset(or_1_out));  // open: Qn, preset, en
  or or_1 (or_1_out, and_1_out, and_3_out);
  J_K_Flip_Flop #(.trigger("falling")) j_k_ff_3 (
    .J(VCC__PIN_5), .clk(Q_B__PIN_9), .K(VCC__PIN_5), .Q(Q_C__PIN_8), .reset(or_2_out));  // open: Qn, preset, en
  or or_2 (or_2_out, and_1_out, and_3_out);
  and and_2 (and_2_out, Q_B__PIN_9, Q_C__PIN_8);
  J_K_Flip_Flop #(.trigger("falling")) j_k_ff_4 (
    .J(and_2_out), .clk(CLK_B__PIN_1), .K(Q_D__PIN_11), .Q(Q_D__PIN_11), .Qn(j_k_ff_4_qn),
    .preset(and_1_out), .reset(and_3_out));  // open: en
  and and_3 (and_3_out, R1__PIN_2, R2__PIN_3);

  // Notes on the sheet:
  //   74LS90 IC (DECADE COUNTER)
endmodule

module IC_74LS74 (
  input  _1CLK__PIN_3,
  input  _2CLK__PIN11,
  input  _1D__PIN_2,
  input  _2D__PIN_12,
  input  _1SET_prime___PIN_4,
  input  _1RST_prime__PIN_1,
  input  _2SET_prime__PIN_10,
  input  in_8,
  output _2Q__PIN_9,
  output _2Q_prime__PIN_8,
  output _1Q__PIN_5,
  output _1Q_prime__PIN_6
);

  wire not_1_out, not_2_out, not_3_out, not_4_out;

  not not_1 (not_1_out, _1SET_prime___PIN_4);
  D_Flip_Flop d_ff_1 (
    .clk(_1CLK__PIN_3), .D(_1D__PIN_2), .Q(_1Q__PIN_5), .Qn(_1Q_prime__PIN_6), .preset(not_1_out),
    .reset(not_2_out));  // open: en
  not not_2 (not_2_out, _1RST_prime__PIN_1);
  not not_3 (not_3_out, _2SET_prime__PIN_10);
  D_Flip_Flop d_ff_2 (
    .clk(_2CLK__PIN11), .D(_2D__PIN_12), .Q(_2Q__PIN_9), .Qn(_2Q_prime__PIN_8), .preset(not_3_out),
    .reset(not_4_out));  // open: en
  not not_4 (not_4_out, in_8);

  // Notes on the sheet:
  //   74LS74 IC (DUAL D FLIP-FLOPS)
  //   2RST' (PIN 13)
endmodule

module IC_74LS47 (
  input  A__PIN_7,
  input  B__PIN_1,
  input  C__PIN_2,
  input  D__PIN_6,
  input  BI_prime_RBO_prime__PIN_4,
  input  LT_prime__PIN_3,
  input  RBI_prime__PIN_5,
  output a__PIN_13,
  output b__PIN_12,
  output c___PIN_11,
  output d__PIN_10,
  output e__PIN_9,
  output f__PIN_15,
  output g__PIN_14
);

  wire and_1_out, and_2_out, and_3_out, and_4_out, and_5_out, and_6_out, and_7_out, and_8_out, and_9_out,
       and_10_out, and_11_out, and_12_out, and_13_out, and_14_out, and_15_out, and_16_out, and_17_out,
       buffer_1_out, nand_1_out, nand_2_out, nand_3_out, nand_5_out, nand_6_out, nand_7_out, nand_8_out,
       not_1_out, not_2_out, not_3_out;

  nand nand_1 (nand_1_out, A__PIN_7, not_3_out);
  nand nand_2 (nand_2_out, B__PIN_1, B__PIN_1, not_3_out);
  nand nand_3 (nand_3_out, C__PIN_2, not_3_out);
  not not_1 (not_1_out, D__PIN_6);
  not not_2 (not_2_out, BI_prime_RBO_prime__PIN_4);
  not not_3 (not_3_out, LT_prime__PIN_3);
  nand nand_4 (not_2_out, not_3_out, RBI_prime__PIN_5, not_1_out, nand_3_out, nand_2_out, nand_1_out);
  nand nand_5 (nand_5_out, nand_1_out, not_2_out);
  nand nand_6 (nand_6_out, nand_2_out, not_2_out);
  nand nand_7 (nand_7_out, nand_3_out, not_2_out);
  nand nand_8 (nand_8_out, not_1_out, not_2_out);
  and and_1 (and_1_out, nand_6_out, nand_8_out);
  and and_2 (and_2_out, nand_1_out, nand_7_out);
  and and_3 (and_3_out, nand_5_out, nand_2_out, nand_3_out, not_1_out);
  and and_4 (and_4_out, nand_6_out, nand_8_out);
  and and_5 (and_5_out, nand_5_out, nand_2_out, nand_7_out);
  and and_6 (and_6_out, nand_1_out, nand_6_out, nand_6_out, nand_7_out);
  and and_7 (and_7_out, nand_7_out, nand_8_out);
  and and_8 (and_8_out, nand_1_out, nand_3_out, nand_6_out);
  and and_9 (and_9_out, nand_5_out, nand_2_out, nand_3_out);
  and and_10 (and_10_out, nand_1_out, nand_2_out, nand_7_out);
  and and_11 (and_11_out, nand_5_out, nand_6_out, nand_7_out);
  buf buffer_1 (buffer_1_out, nand_5_out);
  and and_12 (and_12_out, nand_2_out, nand_7_out);
  and and_13 (and_13_out, nand_5_out, nand_6_out);
  and and_14 (and_14_out, nand_6_out, nand_3_out);
  and and_15 (and_15_out, nand_5_out, nand_3_out, not_1_out);
  and and_16 (and_16_out, nand_5_out, nand_6_out, nand_7_out);
  and and_17 (and_17_out, nand_3_out, nand_2_out, not_1_out, not_3_out);
  nor nor_1 (a__PIN_13, and_1_out, and_2_out, and_3_out);
  nor nor_2 (b__PIN_12, and_4_out, and_5_out, and_6_out);
  nor nor_3 (c___PIN_11, and_7_out, and_8_out);
  nor nor_4 (d__PIN_10, and_9_out, and_10_out, and_11_out);
  nor nor_5 (e__PIN_9, buffer_1_out, and_12_out);
  nor nor_6 (f__PIN_15, and_13_out, and_14_out, and_15_out);
  nor nor_7 (g__PIN_14, and_16_out, and_17_out);

  // Notes on the sheet:
  //   BLANKING I/POR RIPPLE BLANKING O/P
  //   LAMP TEST I/P
  //   RIPPLE BLANKING I/P
  //   74LS47 IC (BCD TO 7 SEGMENT DECODER)
  //   NOTE: ACTUAL O/PS ARE ACTIVE LOW
endmodule

module IC_74LS157 (
  input  _1A__PIN_2,
  input  _1B__PIN_3,
  input  _2A__PIN_5,
  input  _2B__PIN_6,
  input  _3A__PIN_11,
  input  _3B__PIN_10,
  input  _4A__PIN_14,
  input  _4B__PIN_13,
  input  in_9,
  input  in_10,
  output _1Y__PIN_4,
  output _2Y__PIN_7,
  output _3Y__PIN_9,
  output _4Y__PIN_12
);

  wire and_1_out, and_2_out, and_3_out, and_4_out, and_5_out, and_6_out, and_7_out, and_8_out, and_9_out,
       and_10_out, not_1_out;

  not not_1 (not_1_out, in_10);
  and and_1 (and_1_out, ~in_9, ~in_10);  // AND_Gate
  and and_2 (and_2_out, ~in_9, ~not_1_out);  // AND_Gate
  and and_3 (and_3_out, _1A__PIN_2, and_1_out);
  and and_4 (and_4_out, _1B__PIN_3, and_2_out);
  and and_5 (and_5_out, _2A__PIN_5, and_1_out);
  and and_6 (and_6_out, _2B__PIN_6, and_2_out);
  and and_7 (and_7_out, _3A__PIN_11, and_1_out);
  and and_8 (and_8_out, _3B__PIN_10, and_2_out);
  and and_9 (and_9_out, _4A__PIN_14, and_1_out);
  and and_10 (and_10_out, _4B__PIN_13, and_2_out);
  or or_1 (_1Y__PIN_4, and_3_out, and_4_out);
  or or_2 (_2Y__PIN_7, and_5_out, and_6_out);
  or or_3 (_3Y__PIN_9, and_7_out, and_8_out);
  or or_4 (_4Y__PIN_12, and_9_out, and_10_out);

  // Notes on the sheet:
  //   STROBE G' (PIN 15)
  //   SELECT A'/B (PIN 1)
  //   74LS157 IC (QUAD 2:1 MUX)
endmodule

module Edge_Detector (
  input  CLK,
  input  BUTTON_INPUT,
  output PULSE_OUTPUT
);

  wire ic_74ls74_1__1q__pin_5, ic_74ls74_1__2q_prime__pin_8;

  IC_74LS74 ic_74ls74_1 (
    ._1D__PIN_2(BUTTON_INPUT), ._2D__PIN_12(ic_74ls74_1__1q__pin_5), ._1CLK__PIN_3(CLK),
    ._1Q__PIN_5(ic_74ls74_1__1q__pin_5), ._2CLK__PIN11(CLK), ._2Q_prime__PIN_8(ic_74ls74_1__2q_prime__pin_8));  // open: _1Q_prime__PIN_6, _2Q__PIN_9, _1SET_prime___PIN_4, _1RST_prime__PIN_1, _2SET_prime__PIN_10, in_8
  and and_1 (PULSE_OUTPUT, ic_74ls74_1__1q__pin_5, ic_74ls74_1__2q_prime__pin_8);

  // Notes on the sheet:
  //   EDGE DETECTOR USING 74LS74 IC (DUAL D FLIP FLOP)
endmodule

module D_FF_Memory_Cell (
  input  RESET,
  input  CLK,
  input  A,
  input  C,
  input  B,
  input  D,
  output A_2,
  output C_2,
  output B_2,
  output D_2
);

  wire not_1_out;

  not not_1 (not_1_out, RESET);
  IC_74LS74 ic_74ls74_1 (
    ._1D__PIN_2(A), ._2D__PIN_12(B), ._1CLK__PIN_3(CLK), ._1Q__PIN_5(A_2), ._2CLK__PIN11(CLK),
    ._2Q__PIN_9(B_2), ._1SET_prime___PIN_4(not_1_out), ._1RST_prime__PIN_1(not_1_out),
    ._2SET_prime__PIN_10(not_1_out), .in_8(not_1_out));  // open: _1Q_prime__PIN_6, _2Q_prime__PIN_8
  IC_74LS74 ic_74ls74_2 (
    ._1D__PIN_2(C), ._2D__PIN_12(D), ._1CLK__PIN_3(CLK), ._1Q__PIN_5(C_2), ._2CLK__PIN11(CLK),
    ._2Q__PIN_9(D_2), ._1SET_prime___PIN_4(not_1_out), ._1RST_prime__PIN_1(not_1_out),
    ._2SET_prime__PIN_10(not_1_out), .in_8(not_1_out));  // open: _1Q_prime__PIN_6, _2Q_prime__PIN_8

  // Notes on the sheet:
  //   4 BIT MEMORY CELL USING 2 74LS74 ICs
endmodule
